# Fritzing sketch circuit (saved by Fritzing 0.9.3b)
breadboards: 1

parts:
  On_Arduino_Uno_Rev3 = Adafruit Motor/Stepper/Servo Shield [part_number="Adafruit #1438"]
  LEFT_MOTOR = DC Motor
  RIGHT_MOTOR = DC Motor
  IR_SENSOR = PHOTOTRANSISTOR REFLECTIVE OBJECT SENSOR [package=qrb1114-side]
  IR_SENSOR_2 = PHOTOTRANSISTOR REFLECTIVE OBJECT SENSOR [package=qrb1114-side]
  220_Ω = Resistor [tolerance=±5% resistance=220 package="1206 [SMD]"]
  100K_Ω = Resistor [tolerance=±5% resistance=220 package="1206 [SMD]"]
  220_Ω_2 = Resistor [tolerance=±5% resistance=220 package="2010 [SMD]"]
  100K_Ω_2 = Resistor [tolerance=±5% resistance=220 package="2010 [SMD]"]
  U3 = LCD-16X2 [package=lcd-16x2]
  220_Ω_3 = Resistor [tolerance=±5% resistance=220 package="1206 [SMD]"]
  10K_Ω = Rotary Potentiometer (Small) [maximum_resistance=100kΩ package=THT]

nets:
  N1: On_Arduino_Uno_Rev3.AD1, IR_SENSOR_2.C, 100K_Ω_2.Pin_0
  N2: On_Arduino_Uno_Rev3.AD0, IR_SENSOR.C, 100K_Ω.Pin_1
  N3: On_Arduino_Uno_Rev3.D2, U3.DB7
  N4: On_Arduino_Uno_Rev3.D4, U3.DB5
  N5: On_Arduino_Uno_Rev3.D5, U3.DB4
  N6: On_Arduino_Uno_Rev3.M2A, RIGHT_MOTOR.pin_1
  N7: On_Arduino_Uno_Rev3.M2B, RIGHT_MOTOR.pin_2
  GND: On_Arduino_Uno_Rev3.GND, IR_SENSOR.E, IR_SENSOR.K, IR_SENSOR_2.E, IR_SENSOR_2.K, U3.VSS, 220_Ω_3.Pin_0
  N8: On_Arduino_Uno_Rev3.M1B, LEFT_MOTOR.pin_2
  N9: On_Arduino_Uno_Rev3.M1A, LEFT_MOTOR.pin_1
  N10: On_Arduino_Uno_Rev3.+5V, 220_Ω.Pin_0, 100K_Ω.Pin_0, 220_Ω_2.Pin_1, 100K_Ω_2.Pin_1
  N11: On_Arduino_Uno_Rev3.D12, U3.RS
  N12: On_Arduino_Uno_Rev3.D3, U3.DB6
  N13: IR_SENSOR.A, 220_Ω.Pin_1
  N14: IR_SENSOR_2.A, 220_Ω_2.Pin_0
  N15: U3.VDD, 10K_Ω.leg2
  N16: U3.VO, 10K_Ω.wiper
  N17: U3.A, 220_Ω_3.Pin_1
  N18: U3.K, 10K_Ω.leg1

custom parts:
  Adafruit Motor/Stepper/Servo Shield: The original Adafruit Motorshield kit is one of our most beloved kits, which is why we decided to make something even better. We have upgraded the shield kit to make the bestest, easiest way to drive DC and Stepper motors. This shield will make quick work of your next robotics project! We kept the ability to drive up to 4 DC motors or 2 stepper motors, but added many improvements: Instead of a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
